# Fritzing sketch MH-Z19C Wiring (saved by Fritzing 1.0.4)

parts:
  A1 = Arduino UNO R4 WiFi
  TD-er1 = MH-Z19 CO2 sensor [part_number=MH-Z19]

nets:
  N1: A1.Pin_8, A1.Pin_27, TD-er1.Vin
  N2: A1.Pin_9, A1.Pin_30, TD-er1.GND
  N3: A1.Pin_36, TD-er1.TX
  N4: A1.Pin_37, TD-er1.RX

custom parts:
  Arduino UNO R4 WiFi: The Arduino UNO R4 WiFi merges the RA4M1 microprocessor from Renesas with the ESP32-S3 from Espressif, creating an all-in-one tool for makers with enhanced processing power and a diverse array of new peripherals.
